// Logisim project cpu.circ as structural Verilog: 1 circuit, main circuit cpu
module cpu (
  input  clk,
  input  [31:0] INSTRUCTION,
  input  [31:0] READ_DATA,
  output [31:0] WRITE_ADDRESS,
  output [31:0] PROGRAM_COUNTER,
  output [31:0] ra,
  output [31:0] sp,
  output [31:0] t0,
  output [31:0] t1,
  output [31:0] t2,
  output [31:0] s0,
  output [31:0] s1,
  output [31:0] a0,
  output [31:0] tohost,
  output [3:0] WRITE_ENABLE,
  output [31:0] WRITE_DATA
);

  wire ASel, BrEq, BrLt, BrUn, BSel, RegWEn;
  wire [1:0] WBSel;
  wire [2:0] ImmSel;
  wire [3:0] ALUSel;
  wire [31:0] adder_1_out, ALUOut, IF_ID_INSTRUCTION, IF_ID_PC, imm, multiplexer_1_out, multiplexer_2_out,
       Read_Data_1, Read_Data_2, Write_Data_Reg;

  Adder #(.width(32)) adder_1 (.a(PROGRAM_COUNTER), .b(32'h4), .out(adder_1_out));  // open: cin, cout
  Register #(.width(32)) PC (.D(adder_1_out), .clk(clk), .Q(PROGRAM_COUNTER));  // open: en, clr
  control_logic control_logic_1 (
    .RegWEn(RegWEn), .ImmSel(ImmSel), .BrUn(BrUn), .ASel(ASel), .BSel(BSel), .ALUSel(ALUSel), .WBSel(WBSel),
    .inst(IF_ID_INSTRUCTION), .BrEq(BrEq), .BrLt(BrLt));  // open: CSRWen, PCSel, MemRW, CSRSel
  Register #(.width(32)) register_1 (.D(PROGRAM_COUNTER), .clk(clk), .Q(IF_ID_PC));  // open: en, clr
  Register #(.width(32)) register_2 (.D(INSTRUCTION), .clk(clk), .Q(IF_ID_INSTRUCTION));  // open: en, clr
  csr csr_1 (.tohost(tohost));  // open: CSR_address, CSR_din, CSR_WE, clk
  imm_gen imm_gen_1 (.inst(IF_ID_INSTRUCTION), .ImmSel(ImmSel), .imm(imm));
  regfile regfile_1 (
    .rs1(IF_ID_INSTRUCTION[19:15]), .rs2(IF_ID_INSTRUCTION[24:20]), .rd(IF_ID_INSTRUCTION[11:7]),
    .Write_Data(Write_Data_Reg), .RegWEn(RegWEn), .clk(clk), .ra(ra), .sp(sp), .t0(t0), .t1(t1), .t2(t2),
    .s0(s0), .s1(s1), .a0(a0), .Read_Data_1(Read_Data_1), .Read_Data_2(Read_Data_2));
  branch_comp branch_comp_1 (.rs1(Read_Data_1), .rs2(Read_Data_2), .BrUn(BrUn), .BrEq(BrEq), .BrLt(BrLt));
  Multiplexer #(.enable("false"), .width(32)) multiplexer_1 (
    .in0(Read_Data_1), .in1(PROGRAM_COUNTER), .out(multiplexer_1_out), .sel(ASel));
  Multiplexer #(.enable("false"), .width(32)) multiplexer_2 (
    .in0(Read_Data_2), .in1(imm), .out(multiplexer_2_out), .sel(BSel));
  alu alu_1 (.Result(ALUOut), .A(multiplexer_1_out), .B(multiplexer_2_out), .ALUSel(ALUSel));
  Multiplexer #(.enable("false"), .select(2), .width(32)) multiplexer_3 (
    .in0(ALUOut), .in3(READ_DATA), .out(Write_Data_Reg), .sel(WBSel));  // open: in1, in2

  // Other names for the same wires on the sheet: opt_code[6:0] = IF_ID_INSTRUCTION[6:0];
  //   rd[4:0] = IF_ID_INSTRUCTION[11:7]; rs1[4:0] = IF_ID_INSTRUCTION[19:15]; rs2[4:0] = IF_ID_INSTRUCTION[24:20]

  // Notes on the sheet:
  //   Output to IMEM
  //   IMEM (do **NOT** move this)
  //   Inputs from IMEM
  //   It is OK to move the PC, RegFile, ALU, MEM, Branch Comp, Imm Gen, and Control Logic to wherever is most convenient for you when constructing your CPU, and to delete this text
  //   Inputs/Outputs for testing. Do **NOT** move these.
  //   Outputs To DMEM
  //   DMEM (do **NOT** move this)
  //   Inputs From DMEM
endmodule
